// Logisim project Lab 2 Given.circ as structural Verilog: 11 circuits, main circuit Main
module Main (
);

  wire alu_1_zero, ALUOp, ALUSrc, Branch, Clock, JAL, JR, Jump, MemRead, MemToReg, MemWrite, PCSrc, RegDst,
       RegWrite;
  wire [3:0] ALUCtl;
  wire [4:0] _20_16, multiplexer_3_out, WrAddr;
  wire [5:0] _5_0, _31_26;
  wire [15:6] _15_0;
  wire [25:21] _25_0;
  wire [31:0] adder_2_out, alu_1_aluresult, data_memory_1_dataout, multiplexer_1_out, multiplexer_2_out,
       pc_1_pcout, PC_4, register_file_1_rddata1, register_file_1_rddata2, shifter_1_out, SignExtend, WrData;

  PC pc_1 (.PCin(multiplexer_1_out), .PCout(pc_1_pcout), .Clock(Clock));
  Clock u_Clock (.out(Clock));
  // Probe on pc_1_pcout
  Instruction_Mem instruction_mem_1 (.In(pc_1_pcout[7:0]), .Instruction({_31_26, _25_0, _20_16, _15_0, _5_0}));
  // Probe on PC_4
  Adder #(.width(32)) adder_1 (.a(pc_1_pcout), .b(32'h4), .out(PC_4));  // open: cin, cout
  Control_Unit control_unit_1 (
    .In(_31_26), .Branch(Branch), .MemRead(MemRead), .MemtoReg(MemToReg), .MemWrite(MemWrite),
    .ALUSrc(ALUSrc), .RegWrite(RegWrite), .RegDst(RegDst), .ALUOp(ALUOp), .Jump(Jump), .JR(JAL), .JAL(JR));
  Shifter #(.width(32)) shifter_1 (.in(SignExtend), .\dist (5'b00010), .out(shifter_1_out));
  Sign_Extend sign_extend_1 (.In({_15_0, _5_0}), .Out(SignExtend));
  // Probe on shifter_1_out
  Adder #(.width(32)) adder_2 (.a(PC_4), .b(shifter_1_out), .out(adder_2_out));  // open: cin, cout
  // Probe on WrAddr
  Register_File register_file_1 (
    .WrAddr(WrAddr), .WrData(WrData), .WrReg(RegWrite), .RdAddr1(_25_0), .RdAddr2(_20_16),
    .RdData1(register_file_1_rddata1), .RdData2(register_file_1_rddata2));  // open: Clock
  // Probe on WrData
  ALU_Control alu_control_1 (.In(_5_0), .Out(ALUCtl), .ALUOp(ALUOp));
  Multiplexer #(.width(32), .enable("false")) multiplexer_1 (
    .in0(PC_4), .in1(adder_2_out), .out(multiplexer_1_out), .sel(PCSrc));
  Multiplexer #(.width(32), .enable("false")) multiplexer_2 (
    .in0(register_file_1_rddata2), .in1(SignExtend), .out(multiplexer_2_out), .sel(ALUSrc));
  // Probe on register_file_1_rddata2
  ALU alu_1 (
    .ALUCtl(ALUCtl), .A(register_file_1_rddata1), .B(multiplexer_2_out), .ALUResult(alu_1_aluresult),
    .Zero(alu_1_zero), .Shamt({5{1'b0}}));  // open: Overflow
  Multiplexer #(.width(5)) multiplexer_3 (
    .in0(_20_16), .in1(_15_0[15:11]), .out(multiplexer_3_out), .sel(RegDst));  // open: en
  and and_1 (PCSrc, alu_1_zero, Branch);
  Multiplexer #(.width(5)) multiplexer_4 (
    .in0(multiplexer_3_out), .in1({5{1'b1}}), .out(WrAddr), .sel(JAL));  // open: en
  Data_Memory data_memory_1 (
    .Address(alu_1_aluresult[7:0]), .Data(register_file_1_rddata2), .MemWrite(MemWrite), .Clock(Clock),
    .DataOut(data_memory_1_dataout), .MemRead(MemRead));
  // Probe on Branch
  // Probe on RegWrite
  Multiplexer #(.width(32), .enable("false")) multiplexer_5 (
    .in0(alu_1_aluresult), .in1(data_memory_1_dataout), .out(WrData), .sel(MemToReg));
  // Probe on Jump
  // Probe on MemWrite
  // Probe on JAL
  // Probe on JR

  // Other names for the same wires on the sheet: _15_0[5:0] = _5_0; _25_0[20:0] = {_20_16, _15_0, _5_0};
  //   _15_11[4:0] = _15_0[15:11]; _25_21[4:0] = _25_0

  // Notes on the sheet:
  //   1F is for Reg31
  //   Note:
  //   JR is jump to RS(25-21) but this is 5 bits
  //   PC is 32 bits. How do we extend?
  //   Note:
  //   If JAL, WrAddr is Reg 31
  //   Note:
  //   JAL Requires the next intructions' address to be put in WrData
  //   Where is this address?
endmodule

module _32_Bit_Adder_Subtractor (
  input  Add_Sub_control,
  input  [31:0] in_2,
  input  [31:0] in_3,
  output [31:0] out_4,
  output carry_out
);

  wire adder_1_cout, subtractor_1_bout;
  wire [31:0] adder_1_out, subtractor_1_out;

  Adder #(.width(32)) adder_1 (.a(in_2), .b(in_3), .out(adder_1_out), .cout(adder_1_cout));  // open: cin
  Subtractor #(.width(32)) subtractor_1 (
    .a(in_2), .b(in_3), .out(subtractor_1_out), .bout(subtractor_1_bout));  // open: bin
  Multiplexer #(.width(32), .enable("false")) multiplexer_1 (
    .in0(adder_1_out), .in1(subtractor_1_out), .out(out_4), .sel(Add_Sub_control));
  Multiplexer #(.enable("false")) multiplexer_2 (
    .in0(adder_1_cout), .in1(subtractor_1_bout), .out(carry_out), .sel(Add_Sub_control));
endmodule

module ALU (
  input  [3:0] ALUCtl,
  input  [31:0] A,
  input  [31:0] B,
  input  [4:0] Shamt,
  output [31:0] ALUResult,
  output Zero,
  output Overflow
);

  wire comparator_1_lt, comparator_2_lt, comparator_3_eq, comparator_4_eq, or_2_out;
  wire [31:0] Add, And, LessThan, LessThanUnsigned, Nor, Or, ShiftLeft, ShiftRight, Sub, Xor;

  // Probe on ALUCtl
  assign Nor = ~(A | B);  // NOR_Gate nor_1, 32 bits wide
  Adder #(.width(32)) adder_1 (.a(A), .b(B), .out(Add));  // open: cin, cout
  Subtractor #(.width(32)) subtractor_1 (.a(A), .b(B), .out(Sub));  // open: bin, bout
  assign And = A & B;  // AND_Gate and_1, 32 bits wide
  assign Or = A | B;  // OR_Gate or_1, 32 bits wide
  assign Xor = A ^ B;  // XOR_Gate xor_1, 32 bits wide
  Comparator #(.width(32)) comparator_1 (.a(A), .b(B), .lt(comparator_1_lt));  // open: gt, eq
  assign LessThan = {{31{1'b0}}, comparator_1_lt};  // Bit_Extender bit_extender_1
  Shifter #(.width(32)) shifter_1 (.in(B), .\dist (Shamt), .out(ShiftLeft));
  Shifter #(.width(32), .shift("lr")) shifter_2 (.in(B), .\dist (Shamt), .out(ShiftRight));
  Comparator #(.width(32), .mode("unsigned")) comparator_2 (.a(A), .b(B), .lt(comparator_2_lt));  // open: gt, eq
  assign LessThanUnsigned = {{31{1'b0}}, comparator_2_lt};  // Bit_Extender bit_extender_2
  Multiplexer #(.select(4), .width(32), .enable("false")) multiplexer_1 (
    .in0(Or), .in1(LessThanUnsigned), .in2(LessThan), .in3(Add), .in4(Sub), .in5(Xor), .in6(And),
    .in14(ShiftRight), .in15(ShiftLeft), .out(ALUResult), .sel(ALUCtl));  // open: in7, in8, in9, in10, in11, in12, in13
  Comparator #(.width(4)) comparator_3 (.a(4'b0011), .b(ALUCtl), .eq(comparator_3_eq));  // open: gt, lt
  Comparator #(.width(4)) comparator_4 (.a(ALUCtl), .b(4'b0100), .eq(comparator_4_eq));  // open: gt, lt
  Overflow_Unit overflow_unit_1 (
    .Add(comparator_3_eq), .Sub(comparator_4_eq), .ASign(A[31]), .BSign(B[31]), .ResultSign(ALUResult[31]),
    .Overflow(Overflow));
  or or_2 (or_2_out, ALUResult[0], ALUResult[1], ALUResult[2], ALUResult[3], ALUResult[4], ALUResult[5], ALUResult[6], ALUResult[7], ALUResult[8], ALUResult[9], ALUResult[10], ALUResult[11], ALUResult[12], ALUResult[13], ALUResult[14], ALUResult[15], ALUResult[16], ALUResult[17], ALUResult[18], ALUResult[19], ALUResult[20], ALUResult[21], ALUResult[22], ALUResult[23], ALUResult[24], ALUResult[25], ALUResult[26], ALUResult[27], ALUResult[28], ALUResult[29], ALUResult[30], ALUResult[31]);
  not not_1 (Zero, or_2_out);

  // Other names for the same wires on the sheet: ASign = A[31]; ResultSign = ALUResult[31]; BSign = B[31]

  // Notes on the sheet:
  //   ALUCtl for ADD for top port
  //   ALUCtl for SUB for second port
endmodule

module Register_File (
  input  [4:0] WrAddr,
  input  [31:0] WrData,
  input  WrReg,
  input  [4:0] RdAddr1,
  input  [4:0] RdAddr2,
  input  Clock,
  output [31:0] RdData1,
  output [31:0] RdData2
);

  wire WrReg0, WrReg1, WrReg2, WrReg3, WrReg4, WrReg5, WrReg6, WrReg7, WrReg8, WrReg9, WrReg10, WrReg11,
       WrReg12, WrReg13, WrReg14, WrReg15, WrReg16, WrReg17, WrReg18, WrReg19, WrReg20, WrReg21, WrReg22,
       WrReg23, WrReg24, WrReg25, WrReg26, WrReg27, WrReg28, WrReg29, WrReg30, WrReg31;
  wire [31:0] RegData1, RegData2, RegData3, RegData4, RegData5, RegData6, RegData7, RegData8, RegData9,
       RegData10, RegData11, RegData12, RegData13, RegData14, RegData15, RegData16, RegData17, RegData18,
       RegData19, RegData20, RegData21, RegData22, RegData23, RegData24, RegData25, RegData26, RegData27,
       RegData28, RegData29, RegData30, RegData31;

  Demultiplexer #(.select(5), .enable("false")) demultiplexer_1 (
    .out0(WrReg0), .out1(WrReg1), .out2(WrReg2), .out3(WrReg3), .out4(WrReg4), .out5(WrReg5), .out6(WrReg6),
    .out7(WrReg7), .out8(WrReg8), .out9(WrReg9), .out10(WrReg10), .out11(WrReg11), .out12(WrReg12),
    .out13(WrReg13), .out14(WrReg14), .out15(WrReg15), .out16(WrReg16), .out17(WrReg17), .out18(WrReg18),
    .out19(WrReg19), .out20(WrReg20), .out21(WrReg21), .out22(WrReg22), .out23(WrReg23), .out24(WrReg24),
    .out25(WrReg25), .out26(WrReg26), .out27(WrReg27), .out28(WrReg28), .out29(WrReg29), .out30(WrReg30),
    .out31(WrReg31), .in(WrReg), .sel(WrAddr));
  // Probe on RegData4
  Register #(.width(32)) Reg4 (.D(WrData), .en(WrReg4), .Q(RegData4), .clk(Clock));  // open: clr
  // Probe on RegData8
  Register #(.width(32)) Reg8 (.D(WrData), .en(WrReg8), .Q(RegData8), .clk(Clock));  // open: clr
  // Probe on RegData12
  Register #(.width(32)) Reg12 (.D(WrData), .en(WrReg12), .Q(RegData12), .clk(Clock));  // open: clr
  // Probe on RegData16
  Register #(.width(32)) Reg16 (.D(WrData), .en(WrReg16), .Q(RegData16), .clk(Clock));  // open: clr
  // Probe on RegData20
  Register #(.width(32)) Reg20 (.D(WrData), .en(WrReg20), .Q(RegData20), .clk(Clock));  // open: clr
  // Probe on RegData24
  Register #(.width(32)) Reg24 (.D(WrData), .en(WrReg24), .Q(RegData24), .clk(Clock));  // open: clr
  // Probe on RegData28
  Register #(.width(32)) Reg28 (.D(WrData), .en(WrReg28), .Q(RegData28), .clk(Clock));  // open: clr
  Register #(.width(32)) Reg1 (.D(WrData), .en(WrReg1), .Q(RegData1), .clk(Clock));  // open: clr
  Register #(.width(32)) Reg5 (.D(WrData), .en(WrReg5), .Q(RegData5), .clk(Clock));  // open: clr
  Register #(.width(32)) Reg9 (.D(WrData), .en(WrReg9), .Q(RegData9), .clk(Clock));  // open: clr
  Register #(.width(32)) Reg13 (.D(WrData), .en(WrReg13), .Q(RegData13), .clk(Clock));  // open: clr
  Register #(.width(32)) Reg17 (.D(WrData), .en(WrReg17), .Q(RegData17), .clk(Clock));  // open: clr
  Register #(.width(32)) Reg21 (.D(WrData), .en(WrReg21), .Q(RegData21), .clk(Clock));  // open: clr
  Register #(.width(32)) Reg25 (.D(WrData), .en(WrReg25), .Q(RegData25), .clk(Clock));  // open: clr
  Register #(.width(32)) Reg29 (.D(WrData), .en(WrReg29), .Q(RegData29), .clk(Clock));  // open: clr
  // Probe on RegData1
  // Probe on RegData5
  // Probe on RegData9
  // Probe on RegData13
  // Probe on RegData17
  // Probe on RegData21
  // Probe on RegData25
  // Probe on RegData29
  // Probe on RegData2
  Register #(.width(32)) Reg2 (.D(WrData), .en(WrReg2), .Q(RegData2), .clk(Clock));  // open: clr
  // Probe on RegData6
  Register #(.width(32)) Reg6 (.D(WrData), .en(WrReg6), .Q(RegData6), .clk(Clock));  // open: clr
  // Probe on RegData10
  Register #(.width(32)) Reg10 (.D(WrData), .en(WrReg10), .Q(RegData10), .clk(Clock));  // open: clr
  // Probe on RegData14
  Register #(.width(32)) Reg14 (.D(WrData), .en(WrReg14), .Q(RegData14), .clk(Clock));  // open: clr
  // Probe on RegData18
  Register #(.width(32)) Reg18 (.D(WrData), .en(WrReg18), .Q(RegData18), .clk(Clock));  // open: clr
  // Probe on RegData22
  Register #(.width(32)) Reg22 (.D(WrData), .en(WrReg22), .Q(RegData22), .clk(Clock));  // open: clr
  // Probe on RegData26
  Register #(.width(32)) Reg26 (.D(WrData), .en(WrReg26), .Q(RegData26), .clk(Clock));  // open: clr
  // Probe on RegData30
  Register #(.width(32)) Reg30 (.D(WrData), .en(WrReg30), .Q(RegData30), .clk(Clock));  // open: clr
  // Probe on RegData3
  Register #(.width(32)) Reg3 (.D(WrData), .en(WrReg3), .Q(RegData3), .clk(Clock));  // open: clr
  // Probe on RegData7
  Register #(.width(32)) Reg7 (.D(WrData), .en(WrReg7), .Q(RegData7), .clk(Clock));  // open: clr
  // Probe on RegData11
  Register #(.width(32)) Reg11 (.D(WrData), .en(WrReg11), .Q(RegData11), .clk(Clock));  // open: clr
  // Probe on RegData15
  Register #(.width(32)) Reg15 (.D(WrData), .en(WrReg15), .Q(RegData15), .clk(Clock));  // open: clr
  // Probe on RegData19
  Register #(.width(32)) Reg19 (.D(WrData), .en(WrReg19), .Q(RegData19), .clk(Clock));  // open: clr
  // Probe on RegData23
  Register #(.width(32)) Reg23 (.D(WrData), .en(WrReg23), .Q(RegData23), .clk(Clock));  // open: clr
  // Probe on RegData27
  Register #(.width(32)) Reg27 (.D(WrData), .en(WrReg27), .Q(RegData27), .clk(Clock));  // open: clr
  // Probe on RegData31
  Register #(.width(32)) Reg31 (.D(WrData), .en(WrReg31), .Q(RegData31), .clk(Clock));  // open: clr
  Multiplexer #(.select(5), .width(32), .enable("false")) multiplexer_1 (
    .in0({32{1'b0}}), .in1(RegData1), .in2(RegData2), .in3(RegData3), .in4(RegData4), .in5(RegData5),
    .in6(RegData6), .in7(RegData7), .in8(RegData8), .in9(RegData9), .in10(RegData10), .in11(RegData11),
    .in12(RegData12), .in13(RegData13), .in14(RegData14), .in15(RegData15), .in16(RegData16),
    .in17(RegData17), .in18(RegData18), .in19(RegData19), .in20(RegData20), .in21(RegData21),
    .in22(RegData22), .in23(RegData23), .in24(RegData24), .in25(RegData25), .in26(RegData26),
    .in27(RegData27), .in28(RegData28), .in29(RegData29), .in30(RegData30), .in31(RegData31), .out(RdData1),
    .sel(RdAddr1));
  Multiplexer #(.select(5), .width(32), .enable("false")) multiplexer_2 (
    .in0({32{1'b0}}), .in1(RegData1), .in2(RegData2), .in3(RegData3), .in4(RegData4), .in5(RegData5),
    .in6(RegData6), .in7(RegData7), .in8(RegData8), .in9(RegData9), .in10(RegData10), .in11(RegData11),
    .in12(RegData12), .in13(RegData13), .in14(RegData14), .in15(RegData15), .in16(RegData16),
    .in17(RegData17), .in18(RegData18), .in19(RegData19), .in20(RegData20), .in21(RegData21),
    .in22(RegData22), .in23(RegData23), .in24(RegData24), .in25(RegData25), .in26(RegData26),
    .in27(RegData27), .in28(RegData28), .in29(RegData29), .in30(RegData30), .in31(RegData31), .out(RdData2),
    .sel(RdAddr2));
endmodule

module Overflow_Unit (
  input  Add,
  input  Sub,
  input  ASign,
  input  BSign,
  input  ResultSign,
  output Overflow
);

  wire and_1_out, and_2_out, or_1_out, xnor_1_out, xor_1_out, xor_2_out;

  xnor xnor_1 (xnor_1_out, ASign, BSign);
  xor xor_1 (xor_1_out, ASign, BSign);
  and and_1 (and_1_out, xnor_1_out, Add);
  and and_2 (and_2_out, xor_1_out, Sub);
  or or_1 (or_1_out, and_1_out, and_2_out);
  xor xor_2 (xor_2_out, ResultSign, ASign);
  and and_3 (Overflow, or_1_out, xor_2_out);

  // Notes on the sheet:
  //   Overflow occurs when doing addition and sign(A) == sign(B) && sign(result) != sign(A)
  //   Or
  //   Overflow occurs when doing subtraction and sign(A) != sign(B) && sign(result) != sign(A)
endmodule

module PC (
  input  [31:0] PCin,
  input  Clock,
  output [31:0] PCout
);

  Register #(.width(32)) register_1 (.D(PCin), .Q(PCout), .clk(Clock));  // open: en, clr
endmodule

module Instruction_Mem (
  input  [7:0] In,
  output [31:0] Instruction
);

  ROM #(.dataWidth(32)) rom_1 (.addr(In), .data(Instruction));  // open: sel

  // Notes on the sheet:
  //   contents of rom_1 (hex, n*v repeats v):
  //   20010008 34220005 3043ffff 612020 832822 223024 c33826 aca40064 8ca80064 22482a 1265025 214bfff6
  //   10b602b c00000f 200d0001 23ff0018 10c00003 a13022 8000010 200e0001 3e00008 200f0001 20100001
endmodule

module Data_Memory (
  input  [7:0] Address,
  input  [31:0] Data,
  input  MemWrite,
  input  MemRead,
  input  Clock,
  output [31:0] DataOut
);

  RAM #(.dataWidth(32), .bus("separate")) ram_1 (
    .addr(Address), .din(Data), .data(DataOut), .str(MemWrite), .clk(Clock), .ld(MemRead));  // open: sel, clr
endmodule

module Control_Unit (
  input  [5:0] In,
  output Branch,
  output MemRead,
  output MemtoReg,
  output MemWrite,
  output ALUSrc,
  output RegWrite,
  output RegDst,
  output ALUOp,
  output Jump,
  output JR,
  output JAL
);

  wire and_5_out, and_6_out, and_7_out, not_1_out, not_2_out, not_3_out, not_4_out, not_5_out, not_6_out,
       not_7_out, not_8_out, not_9_out, not_10_out, not_11_out, not_12_out, not_13_out, not_14_out;

  not not_1 (not_1_out, In[2]);
  not not_2 (not_2_out, In[2]);
  not not_3 (not_3_out, In[2]);
  and and_1 (MemWrite, In[2], In[4]);
  or or_1 (ALUSrc, In[2], In[0]);
  not not_4 (not_4_out, In[3]);
  not not_5 (not_5_out, In[4]);
  not not_6 (not_6_out, In[4]);
  not not_7 (not_7_out, In[2]);
  not not_8 (not_8_out, In[2]);
  not not_9 (not_9_out, In[3]);
  not not_10 (not_10_out, In[4]);
  not not_11 (not_11_out, In[4]);
  not not_12 (not_12_out, In[5]);
  not not_13 (not_13_out, In[0]);
  not not_14 (not_14_out, In[2]);
  and and_2 (Branch, not_1_out, In[3]);
  and and_3 (MemRead, In[0], not_2_out);
  and and_4 (MemtoReg, In[0], not_3_out);
  and and_5 (and_5_out, not_4_out, not_5_out);
  and and_6 (and_6_out, In[2], not_6_out);
  and and_7 (and_7_out, In[0], not_7_out);
  and and_8 (RegDst, not_8_out, not_9_out, not_10_out);
  or or_2 (ALUOp, not_11_out, In[0]);
  and and_9 (Jump, In[4], not_12_out);
  and and_10 (JAL, not_13_out, not_14_out, In[5]);
  or or_3 (RegWrite, and_5_out, and_6_out, and_7_out);

  assign JR = 1'b0;
endmodule

module Sign_Extend (
  input  [15:0] In,
  output [31:0] Out
);

  assign Out = {{16{In[15]}}, In};  // Bit_Extender bit_extender_1
endmodule

module ALU_Control (
  input  ALUOp,
  input  [5:0] In,
  output [3:0] Out
);

  wire and_1_out, and_2_out, and_3_out, and_4_out, and_5_out, not_1_out, not_2_out, not_3_out, not_4_out,
       not_5_out, not_6_out;
  wire [3:1] or_1_out;

  not not_1 (not_1_out, In[2]);
  and and_1 (and_1_out, not_1_out, In[4]);
  and and_2 (and_2_out, In[3], not_2_out);
  not not_2 (not_2_out, In[5]);
  not not_3 (not_3_out, In[4]);
  and and_3 (and_3_out, not_3_out, not_4_out);
  not not_4 (not_4_out, In[5]);
  not not_5 (not_5_out, In[3]);
  and and_4 (and_4_out, not_5_out, not_6_out);
  not not_6 (not_6_out, In[4]);
  and and_5 (and_5_out, In[3], In[4]);
  or or_1 (or_1_out[1], and_1_out, and_2_out);
  or or_2 (or_1_out[2], and_3_out, In[2]);
  or or_3 (or_1_out[3], and_4_out, and_5_out);
  Multiplexer #(.width(4), .enable("false")) multiplexer_1 (
    .in0(4'b0000), .in1({or_1_out, 1'b0}), .out(Out), .sel(ALUOp));
endmodule
